# Fritzing sketch Dendrometer (saved by Fritzing 0.9.4)
breadboards: 1

parts:
  U1 = SHT1x Humdity Sensor [package=sht1x]
  Part1 = Adafruit Feather M0 RFM9x LoRa [part_number="Adafruit #3178 or #3179"]
  U2 = SHT1x Humdity Sensor [package=sht1x]  # not connected

nets:
  GND: U1.GND
  N1: U1.DATA, Part1.SDA
  N2: U1.SCK, Part1.SCL

custom parts:
  Adafruit Feather M0 RFM9x LoRa: This is the Adafruit Feather M0 RFM95 LoRa Radio - our take on an microcontroller with a "Long Range (LoRa)" packet radio transceiver with built in USB and battery charging. Its an Adafruit Feather M0 with a 433Mhz or 900MHz radio module cooked in! Great for making wireless networks that are more flexible than Bluetooth LE and without the high power requirements of WiFi. We have other boards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
